# Fritzing sketch MQ2 (saved by Fritzing 0.9.3b)
breadboards: 1

parts:
  Componente1 = Arduino Uno (Rev3)
  Componente2 = MQ-9 breakout
  J1 = Piezo Speaker
  LED1 = LED - 5mm [color="Red (633nm)" package="5 mm [THT]"]
  LED2 = LEDs [package=led10mm]
  R1 = Resistor [tolerance=±5% resistance=220 package="0805 [SMD]"]
  R2 = Resistor [tolerance=±5% resistance=220 package="0805 [SMD]"]

nets:
  N1: Componente1.A0, Componente2.AO
  N2: Componente1.D2, Componente2.DO
  N3: Componente1.D3_PWM, R1.Pin_1
  N4: Componente1.D4, R2.Pin_1
  N5: Componente1.D5_PWM, J1.pin2
  5V: Componente1.5V, Componente2.VCC
  GND: Componente1.GND, Componente2.GND, J1.pin1, LED1.cathode, LED2.C
  N6: LED1.anode, R1.Pin_0
  N7: LED2.A, R2.Pin_0

custom parts:
  MQ-9 breakout: SKU: 101284
